# Fritzing sketch FritzSketch (saved by Fritzing 0.8.7b)
breadboards: 1

parts:
  Part1 = Arduino Uno (Rev3)
  J1 = Basic Force Sensing Resistor (FSR) [package=THT]
  J2 = Basic Force Sensing Resistor (FSR) [package=THT]
  R1 = Resistor [tolerance=±5% resistance=220 package=THT]
  R2 = Resistor [tolerance=±5% resistance=10k package=THT]

nets:
  N1: Part1.A0, J1.pin_1, R2.Pin_0
  N2: Part1.A1, J2.pin_1, R1.Pin_0
  N3: Part1.5V, J1.pin_0, J2.pin_0
  N4: Part1.GND, R1.Pin_1, R2.Pin_1
